# Fritzing sketch ArduinoOpenLog (saved by Fritzing 0.7.7b)
breadboards: 1

parts:
  VCC1 = Battery block 9V
  S1 = Pushbutton [package="[SMD]"]
  LED1 = LED - 3mm [color="Green (570nm)" package="3 mm [THT]"]
  R1 = Resistor [tolerance=±5% resistance=10k package=THT]
  Part1 = Arduino Pro Mini 3.3V
  U2 = Voltage Regulator - 5V [package="TO220 [THT]"]
  R2 = Resistor [tolerance=±5% resistance=100 package=THT]
  R3 = Basic Force Sensing Resistor (FSR) [package=THT]
  Part2 = OpenLog
  LED2 = LED - 3mm [color="Red (633nm)" package="3 mm [THT]"]

nets:
  N1: VCC1.-, LED1.cathode, R1.Pin_1, U2.GND
  N2: VCC1.+, U2.input_voltage
  N3: S1.Pin_1, S1.Pin_2
  VCC: S1.Pin_3, S1.Pin_4, R1.Pin_0, Part1.VCC, Part1.D6, U2.output_voltage, R3.pin_1, Part2.VCC
  N4: LED1.anode, Part1.D9
  N5: Part1.DTR, Part2.DTR
  N6: Part1.TXO, Part2.RXI
  N7: Part1.RXI, Part2.TXO
  GND: Part1.GND, R2.Pin_0, Part2.GND, LED2.cathode
  N8: Part1.A0, R2.Pin_1, R3.pin_0
  N9: Part1.MISO, LED2.anode
